# Fritzing sketch data (saved by Fritzing 0.9.1b)

parts:
  Raspberry_Pi1 = Raspberry Pi B+
  Part1 = Adafruit FONA - Mini Cellular GSM Breakout
  MIC1 = Microphone
  SP1 = SPEAKER [package=pcb_mount_speaker]

nets:
  N1: Raspberry_Pi1.GPIO4, Part1.RI_5V
  N2: Raspberry_Pi1.GPIO15, Part1.TXD_5V
  N3: Raspberry_Pi1.GPIO14, Part1.RXD_5V
  N4: Part1.VCCIO, Part1.VBAT
  N5: Part1.SPEAKER2-, SP1.+
  N6: Part1.SPEAKER2+, SP1.-
  N7: Part1.MIC2+, MIC1.pin2
  N8: Part1.MIC2-, MIC1.pin1

custom parts:
  Adafruit FONA - Mini Cellular GSM Breakout: An all-in-one cellular phone module that lets you add voice, text, SMS and GPRS data to your project. Quad-band 850/900/1800/1900MHz - connect onto any global GSM network with any 2G SIM. Includes an onboard LiPoly battery charging circuitry so you can take your project on the go. Also works as an FM radio receiver.
